# Fritzing sketch schema (saved by Fritzing 0.9.2b)
circuit board: 10.3178cm x 5.69486cm
breadboards: 2

parts:
  RHT2 = Humidity and Temperature Sensor RHT03
  R3 = Resistor [tolerance=±5% resistance=220 package=THT]
  LED1 = Super Flux LED blue [color=Blue]
  RHT1 = Humidity and Temperature Sensor RHT03
  R4 = Resistor [tolerance=±5% resistance=220 package=THT]
  R5 = Resistor [tolerance=±5% resistance=220 package=THT]
  part = Real Time Clock Module - DS1307 RTC Breakout Board
  part_2 = microSD Socket [package="Molex 502774-0891 [SMD]"]
  part_3 = Arduino Nano (Rev3.0)

nets:
  VCC: RHT2.Vcc, RHT1.Vcc, R4.Pin_1, R5.Pin_1, part_3.3V3
  N1: RHT2.Data-signal, R5.Pin_0, part_3.D3
  GND: RHT2.GND_2, LED1.cathode, RHT1.GND_2, part.GND, part_2.GND, part_3.GND
  N2: R3.Pin_0, part_3.D8
  N3: R3.Pin_1, LED1.anode
  N4: RHT1.Data-signal, R4.Pin_0, part_3.D2
  5V: part.5V, part_3.5V
  N5: part.SCL, part_3.A5
  N6: part.SDA, part_3.A4
  N7: part_2.CS, part_3.D10
  N8: part_2.DI, part_3.D11/MOSI
  N9: part_2.SCK, part_3.D13/SCK
  N10: part_2.DO, part_3.D12/MISO
